# Fritzing sketch 1 (saved by Fritzing 0.9.2b)
breadboards: 1

parts:
  R1 = Resistor [tolerance=±5% resistance=10M package=THT]
  R2 = Resistor [tolerance=±5% resistance=330k package=THT]
  V1 = AC Power [voltage=220 frequency=50]
  C1 = Ceramic Capacitor [capacitance=4.7µF package="100 mil [THT, multilayer]"]
  D1 = Rectifier Diode [part_number=1N4001 package="300 mil [THT]"]
  U1 = Optocoupler [package=THT]
  R3 = Resistor [tolerance=±5% resistance=430k package=THT]
  R4 = Resistor [tolerance=±5% resistance=10M package=THT]
  S1 = Pushbutton [package="[THT]"]
  R5 = Resistor [tolerance=±5% resistance=220 package=THT]
  VCC1 = Battery

nets:
  N1: R1.Pin_0, V1.V+
  N2: R1.Pin_1, R2.Pin_0, D1.cathode
  N3: R2.Pin_1, V1.V-, C1.1
  N4: C1.0, D1.anode, U1.Pin_5
  N5: U1.Pin_1, R5.Pin_0
  N6: U1.Pin_2, S1.Pin_3, S1.Pin_4
  N7: U1.Pin_4, R3.Pin_1, R4.Pin_0
  N8: U1.Pin_6, R3.Pin_0
  N9: S1.Pin_1, S1.Pin_2, VCC1.-
  N10: R5.Pin_1, VCC1.+
